# Fritzing sketch scrawly_wally_wiring (saved by Fritzing 1.0.1rc)

parts:
  MCU1 = Raspberry Pi Zero
  Driver1 = 28BYJ-48 Driver Module [part_number=ULN2003 package=THT]
  SM1 = 28BYJ-48 Stepper Motor [part_number=28BYJ-48]  # not connected
  Driver2 = 28BYJ-48 Driver Module [part_number=ULN2003 package=THT]
  SM2 = 28BYJ-48 Stepper Motor [part_number=28BYJ-48]  # not connected
  J1 = Basic Servo
  Driver3 = 28BYJ-48 Driver Module [part_number=ULN2003 package=THT]  # not connected

nets:
  N1: MCU1.pin_2, MCU1.pin_4, Driver2.Vmotor
  GND: MCU1.pin_6, MCU1.pin_9, MCU1.pin_14, Driver2.GND, J1.gnd
  N2: MCU1.pin_8, Driver1.IN1
  N3: MCU1.pin_10, Driver1.IN2
  N4: MCU1.pin_12, Driver1.IN3
  N5: MCU1.pin_16, Driver1.IN4
  N6: MCU1.pin_18, Driver2.IN1
  N7: MCU1.pin_22, Driver2.IN2
  N8: MCU1.pin_24, Driver2.IN3
  N9: MCU1.pin_26, Driver2.IN4
  N10: MCU1.pin_28, J1.pulse

custom parts:
  28BYJ-48 Driver Module: Generic male header
  28BYJ-48 Stepper Motor: Unipolar Stepper Motor 28BYJ-48 Top coil - pink & orange Bottom coil - blue & yellow Common rail - red Connector pins: blue - pink - yellow - orange - red
